// Logisim project mips-like.circ as structural Verilog: 8 circuits, main circuit PROCESSADOR
module PROCESSADOR (
  output [31:0] \INSTRUÇÃO 
);

  wire and_1_out, button_1_out, clock_1_out, not_1_out, or_1_out, uc_maior_1_branch, uc_maior_1_jump,
       uc_maior_1_mem_to_reg, uc_maior_1_read_mem, uc_maior_1_ula_src, uc_maior_1_write_mem,
       uc_maior_1_write_reg, ula_maior_1_equal;
  wire [1:0] uc_maior_1_ula_op_0;
  wire [3:0] ULA_CONTROL_ula_operation;
  wire [7:0] PC_q_2;
  wire [31:0] adder_1_out, banco_de_registradores_1_r0_d, banco_de_registradores_1_r1_d, bit_extender_1_out,
       bit_extender_2_out, multiplexer_1_out, multiplexer_2_out, multiplexer_3_out, PC_q, ram_1_data,
       ula_maior_1_ula_out;

  Adder #(.width(32)) adder_1 (.a({PC_q[31:10], PC_q_2, PC_q[1:0]}), .b(32'h4), .out(adder_1_out));  // open: cin, cout
  assign bit_extender_1_out = {{16{1'b0}}, \INSTRUÇÃO [15:0]};  // Bit_Extender bit_extender_1
  Multiplexer #(.width(32), .enable("false")) multiplexer_1 (
    .in0(adder_1_out), .in1(bit_extender_1_out), .out(multiplexer_1_out), .sel(or_1_out));
  or or_1 (or_1_out, uc_maior_1_jump, and_1_out);
  and and_1 (and_1_out, uc_maior_1_branch, ~ula_maior_1_equal);  // AND_Gate
  Register #(.width(32)) PC (
    .D(multiplexer_1_out), .Q({PC_q[31:10], PC_q_2, PC_q[1:0]}), .clk(clock_1_out), .clr(button_1_out));  // open: en
  Clock clock_1 (.out(clock_1_out));
  Button button_1 (.out(button_1_out));
  ROM #(.dataWidth(32)) rom_1 (.addr(PC_q_2), .data(\INSTRUÇÃO ));  // open: sel
  UC_MAIOR uc_maior_1 (
    .E3(\INSTRUÇÃO [31]), .ula_op_0(uc_maior_1_ula_op_0[0]), .E2(\INSTRUÇÃO [30]), .E1(\INSTRUÇÃO [29]),
    .E0(\INSTRUÇÃO [28]), .ula_op_1(uc_maior_1_ula_op_0[1]), .write_reg(uc_maior_1_write_reg),
    .write_mem(uc_maior_1_write_mem), .read_mem(uc_maior_1_read_mem), .mem_to_reg(uc_maior_1_mem_to_reg),
    .ula_src(uc_maior_1_ula_src), .jump(uc_maior_1_jump), .branch(uc_maior_1_branch));
  BANCO_DE_REGISTRADORES banco_de_registradores_1 (
    .DATA_WRITE(multiplexer_2_out), .CLK(clock_1_out), .RW(\INSTRUÇÃO [27:24]),
    .R0_D(banco_de_registradores_1_r0_d), .R0(\INSTRUÇÃO [19:16]), .R1_D(banco_de_registradores_1_r1_d),
    .R1(\INSTRUÇÃO [23:20]), .RW_2(uc_maior_1_write_reg), .RESET(button_1_out));
  assign bit_extender_2_out = {{16{1'b0}}, \INSTRUÇÃO [15:0]};  // Bit_Extender bit_extender_2
  Multiplexer #(.width(32), .enable("false")) multiplexer_2 (
    .in0(ula_maior_1_ula_out), .in1(ram_1_data), .out(multiplexer_2_out), .sel(uc_maior_1_mem_to_reg));
  CONTROLE_DE_ULA ULA_CONTROL (
    .OPCODE(\INSTRUÇÃO [31:28]), .ULA_Operation(ULA_CONTROL_ula_operation), .ULA_Option(uc_maior_1_ula_op_0));
  Multiplexer #(.width(32), .enable("false")) multiplexer_3 (
    .in0(banco_de_registradores_1_r1_d), .in1(bit_extender_2_out), .out(multiplexer_3_out),
    .sel(uc_maior_1_ula_src));
  ULA_MAIOR ula_maior_1 (
    .DATA_0(banco_de_registradores_1_r0_d), .DATA_1(multiplexer_3_out), .SHAMT(\INSTRUÇÃO [15:11]),
    .ULA_OUT(ula_maior_1_ula_out), .Equal(ula_maior_1_equal), .ULA_OP(ULA_CONTROL_ula_operation));  // open: Greater, Less
  not not_1 (not_1_out, clock_1_out);
  RAM #(.addrWidth(24), .dataWidth(32), .bus("separate")) ram_1 (
    .addr(ula_maior_1_ula_out[23:0]), .din(banco_de_registradores_1_r1_d), .data(ram_1_data),
    .str(uc_maior_1_write_mem), .clk(not_1_out), .ld(uc_maior_1_read_mem), .clr(button_1_out));  // open: sel

  // Notes on the sheet:
  //   Jump
  //   Branch
  //   Igual da ULA
  //   REG_0
  //   REG_1
  //   REG_W
  //   contents of rom_1 (hex, n*v repeats v):
  //   a100000a 1110000
  //   DATA_W
  //   SHAMT
  //   ADDRESS/IMM
  //   WriteReg
  //   BANCO DE REGISTRADORES
  //   REG0_D
  //   REG1_D
  //   MemToReg (conteúdo da memória vai para o registrador)
  //   ALUSrc
  //   Mem Write
  //   Mem Read
endmodule

module ULA (
  input  [31:0] DATA_0,
  input  [31:0] DATA_1,
  input  ULA_OP,
  output [31:0] ULA_OUT
);

  wire [31:0] adder_1_out, subtractor_1_out;

  Adder #(.width(32)) adder_1 (.a(DATA_0), .b(DATA_1), .out(adder_1_out));  // open: cin, cout
  Subtractor #(.width(32)) subtractor_1 (.a(DATA_0), .b(DATA_1), .out(subtractor_1_out));  // open: bin, bout
  Multiplexer #(.width(32), .enable("false")) multiplexer_1 (
    .in0(adder_1_out), .in1(subtractor_1_out), .out(ULA_OUT), .sel(ULA_OP));
endmodule

module UC (
  input  E3,
  input  E2,
  input  E1,
  input  E0,
  output [1:0] ula_op,
  output write_reg
);
endmodule

module BANCO_DE_REGISTRADORES (
  input  [31:0] DATA_WRITE,
  input  [3:0] R0,
  input  [3:0] R1,
  input  [3:0] RW,
  input  CLK,
  input  RESET,
  input  RW_2,
  output [31:0] R0_D,
  output [31:0] R1_D
);

  wire demultiplexer_1_out0, demultiplexer_1_out1, demultiplexer_1_out2, demultiplexer_1_out3,
       demultiplexer_1_out4, demultiplexer_1_out5, demultiplexer_1_out6, demultiplexer_1_out7,
       demultiplexer_1_out8, demultiplexer_1_out9, demultiplexer_1_out10, demultiplexer_1_out11,
       demultiplexer_1_out12, demultiplexer_1_out13, demultiplexer_1_out14, demultiplexer_1_out15;
  wire [31:0] register_2_q, register_3_q, register_4_q, register_5_q, register_6_q, register_7_q,
       register_8_q, register_9_q, register_10_q, register_11_q, register_12_q, register_13_q, register_14_q,
       register_15_q, register_16_q;

  Register #(.width(32)) register_1 (.D(DATA_WRITE), .en(demultiplexer_1_out0), .clk(CLK), .clr(RESET));  // open: Q
  Register #(.width(32)) register_2 (
    .D(DATA_WRITE), .en(demultiplexer_1_out1), .Q(register_2_q), .clk(CLK), .clr(RESET));
  Register #(.width(32)) register_3 (
    .D(DATA_WRITE), .en(demultiplexer_1_out2), .Q(register_3_q), .clk(CLK), .clr(RESET));
  Demultiplexer #(.select(4), .enable("false")) demultiplexer_1 (
    .out0(demultiplexer_1_out0), .out1(demultiplexer_1_out1), .out2(demultiplexer_1_out2),
    .out3(demultiplexer_1_out3), .out4(demultiplexer_1_out4), .out5(demultiplexer_1_out5),
    .out6(demultiplexer_1_out6), .out7(demultiplexer_1_out7), .out8(demultiplexer_1_out8),
    .out9(demultiplexer_1_out9), .out10(demultiplexer_1_out10), .out11(demultiplexer_1_out11),
    .out12(demultiplexer_1_out12), .out13(demultiplexer_1_out13), .out14(demultiplexer_1_out14),
    .out15(demultiplexer_1_out15), .in(RW_2), .sel(RW));
  Register #(.width(32)) register_4 (
    .D(DATA_WRITE), .en(demultiplexer_1_out3), .Q(register_4_q), .clk(CLK), .clr(RESET));
  Register #(.width(32)) register_5 (
    .D(DATA_WRITE), .en(demultiplexer_1_out4), .Q(register_5_q), .clk(CLK), .clr(RESET));
  Register #(.width(32)) register_6 (
    .D(DATA_WRITE), .en(demultiplexer_1_out5), .Q(register_6_q), .clk(CLK), .clr(RESET));
  Register #(.width(32)) register_7 (
    .D(DATA_WRITE), .en(demultiplexer_1_out6), .Q(register_7_q), .clk(CLK), .clr(RESET));
  Register #(.width(32)) register_8 (
    .D(DATA_WRITE), .en(demultiplexer_1_out7), .Q(register_8_q), .clk(CLK), .clr(RESET));
  Register #(.width(32)) register_9 (
    .D(DATA_WRITE), .en(demultiplexer_1_out8), .Q(register_9_q), .clk(CLK), .clr(RESET));
  Register #(.width(32)) register_10 (
    .D(DATA_WRITE), .en(demultiplexer_1_out9), .Q(register_10_q), .clk(CLK), .clr(RESET));
  Register #(.width(32)) register_11 (
    .D(DATA_WRITE), .en(demultiplexer_1_out10), .Q(register_11_q), .clk(CLK), .clr(RESET));
  Register #(.width(32)) register_12 (
    .D(DATA_WRITE), .en(demultiplexer_1_out11), .Q(register_12_q), .clk(CLK), .clr(RESET));
  Register #(.width(32)) register_13 (
    .D(DATA_WRITE), .en(demultiplexer_1_out12), .Q(register_13_q), .clk(CLK), .clr(RESET));
  Register #(.width(32)) register_14 (
    .D(DATA_WRITE), .en(demultiplexer_1_out13), .Q(register_14_q), .clk(CLK), .clr(RESET));
  Register #(.width(32)) register_15 (
    .D(DATA_WRITE), .en(demultiplexer_1_out14), .Q(register_15_q), .clk(CLK), .clr(RESET));
  Register #(.width(32)) register_16 (
    .D(DATA_WRITE), .en(demultiplexer_1_out15), .Q(register_16_q), .clk(CLK), .clr(RESET));
  Multiplexer #(.select(4), .width(32), .disabled(0), .enable("false")) multiplexer_1 (
    .in0({32{1'b0}}), .in1(register_2_q), .in2(register_3_q), .in3(register_4_q), .in4(register_5_q),
    .in5(register_6_q), .in6(register_7_q), .in7(register_8_q), .in8(register_9_q), .in9(register_10_q),
    .in10(register_11_q), .in11(register_12_q), .in12(register_13_q), .in13(register_14_q),
    .in14(register_15_q), .in15(register_16_q), .out(R0_D), .sel(R0));
  Multiplexer #(.select(4), .width(32), .disabled(0), .enable("false")) multiplexer_2 (
    .in0({32{1'b0}}), .in1(register_2_q), .in2(register_3_q), .in3(register_4_q), .in4(register_5_q),
    .in5(register_6_q), .in6(register_7_q), .in7(register_8_q), .in8(register_9_q), .in9(register_10_q),
    .in10(register_11_q), .in11(register_12_q), .in12(register_13_q), .in13(register_14_q),
    .in14(register_15_q), .in15(register_16_q), .out(R1_D), .sel(R1));

  // Other names for the same wires on the sheet: C = CLK; R = RESET
endmodule

// ULA
module ULA_MAIOR (
  input  [31:0] DATA_0,
  input  [31:0] DATA_1,
  input  [3:0] ULA_OP,
  input  [4:0] SHAMT,
  output [31:0] ULA_OUT,
  output Greater,
  output Equal,
  output Less
);

  wire [31:0] adder_1_out, and_1_out, bit_extender_1_out, bit_extender_2_out, bit_extender_3_out,
       divider_1_out, multiplier_1_out, nand_1_out, negator_1_out, nor_1_out, or_1_out, shifter_1_out,
       shifter_2_out, subtractor_1_out, xnor_1_out, xor_1_out;

  Adder #(.width(32)) adder_1 (.a(DATA_0), .b(DATA_1), .out(adder_1_out));  // open: cin, cout
  Subtractor #(.width(32)) subtractor_1 (.a(DATA_0), .b(DATA_1), .out(subtractor_1_out));  // open: bin, bout
  Multiplier #(.width(32)) multiplier_1 (.a(DATA_0), .b(DATA_1), .out(multiplier_1_out));  // open: cin, cout
  Shifter #(.width(32)) shifter_1 (.in(DATA_0), .\dist (SHAMT), .out(shifter_1_out));
  assign or_1_out = DATA_0 | DATA_1;  // OR_Gate or_1, 32 bits wide
  Comparator #(.width(32), .mode("unsigned")) comparator_1 (
    .a(DATA_0), .b(DATA_1), .gt(Greater), .eq(Equal), .lt(Less));
  Shifter #(.width(32), .shift("lr")) shifter_2 (.in(DATA_0), .\dist (SHAMT), .out(shifter_2_out));
  Divider #(.width(32)) divider_1 (.a(DATA_0), .b(DATA_1), .out(divider_1_out));  // open: upper, rem
  assign and_1_out = DATA_0 & DATA_1;  // AND_Gate and_1, 32 bits wide
  assign nand_1_out = ~(DATA_0 & DATA_1);  // NAND_Gate nand_1, 32 bits wide
  assign nor_1_out = ~(DATA_0 | DATA_1);  // NOR_Gate nor_1, 32 bits wide
  assign xor_1_out = DATA_0 ^ DATA_1;  // XOR_Gate xor_1, 32 bits wide
  Negator #(.width(32)) negator_1 (.in(DATA_0), .out(negator_1_out));
  assign bit_extender_1_out = {{31{1'b0}}, Less};  // Bit_Extender bit_extender_1
  assign bit_extender_2_out = {{31{1'b0}}, Greater};  // Bit_Extender bit_extender_2
  assign xnor_1_out = ~(DATA_0 ^ DATA_1);  // XNOR_Gate xnor_1, 32 bits wide
  assign bit_extender_3_out = {{31{1'b0}}, Equal};  // Bit_Extender bit_extender_3
  Multiplexer #(.select(4), .width(32), .enable("false")) multiplexer_1 (
    .in0(adder_1_out), .in1(subtractor_1_out), .in2(multiplier_1_out), .in3(shifter_1_out), .in4(or_1_out),
    .in5(bit_extender_1_out), .in6(bit_extender_2_out), .in7(bit_extender_3_out), .in8(shifter_2_out),
    .in9(divider_1_out), .in10(and_1_out), .in11(nand_1_out), .in12(nor_1_out), .in13(xor_1_out),
    .in14(xnor_1_out), .in15(negator_1_out), .out(ULA_OUT), .sel(ULA_OP));
endmodule

module PROCESSADOR_MAIOR (
  output [31:0] \INSTRUÇÃO 
);

  wire button_1_out, clock_1_out, UC_write_reg;
  wire [1:0] UC_ula_op;
  wire [31:0] adder_1_out, banco_de_registradores_1_r0_d, banco_de_registradores_1_r1_d, PC_q, ula_1_ula_out;

  Adder #(.width(32)) adder_1 (.a(PC_q), .b(32'h4), .out(adder_1_out));  // open: cin, cout
  Register #(.width(32)) PC (.D(adder_1_out), .Q(PC_q), .clk(clock_1_out), .clr(button_1_out));  // open: en
  Clock clock_1 (.out(clock_1_out));
  Button button_1 (.out(button_1_out));
  ROM #(.dataWidth(32)) rom_1 (.addr(PC_q[9:2]), .data(\INSTRUÇÃO ));  // open: sel
  UC UC (
    .E3(\INSTRUÇÃO [31]), .E2(\INSTRUÇÃO [30]), .E1(\INSTRUÇÃO [29]), .E0(\INSTRUÇÃO [28]),
    .ula_op(UC_ula_op), .write_reg(UC_write_reg));
  BANCO_DE_REGISTRADORES banco_de_registradores_1 (
    .DATA_WRITE(ula_1_ula_out), .CLK(clock_1_out), .RW(\INSTRUÇÃO [27:24]),
    .R0_D(banco_de_registradores_1_r0_d), .R0(\INSTRUÇÃO [19:16]), .R1_D(banco_de_registradores_1_r1_d),
    .R1(\INSTRUÇÃO [23:20]), .RW_2(UC_write_reg), .RESET(button_1_out));
  ULA ula_1 (
    .DATA_0(banco_de_registradores_1_r0_d), .DATA_1(banco_de_registradores_1_r1_d), .ULA_OUT(ula_1_ula_out),
    .ULA_OP(UC_ula_op[0]));
  // Pins of 1 and 2 bits meet at UC_ula_op

  // Notes on the sheet:
  //   REG_0
  //   REG_1
  //   REG_W
  //   contents of rom_1 (hex, n*v repeats v):
  //   120000
  //   DATA_W
  //   SHAMT
  //   ADDRESS/IMM
  //   BANCO DE REGISTRADORES
  //   REG0_D
  //   REG1_D
  //   ULA
endmodule

module CONTROLE_DE_ULA (
  input  [3:0] OPCODE,
  input  [1:0] ULA_Option,
  output [3:0] ULA_Operation
);

  Multiplexer #(.select(2), .width(4), .enable("false")) multiplexer_1 (
    .in0(OPCODE), .in1(4'b0000), .in2(4'b0111), .in3(4'b0100), .out(ULA_Operation), .sel(ULA_Option));

  // Notes on the sheet:
  //   Soma
  //   Igual
  //   Or
endmodule

module UC_MAIOR (
  input  E3,
  input  E2,
  input  E1,
  input  E0,
  output ula_op_0,
  output ula_op_1,
  output write_reg,
  output write_mem,
  output read_mem,
  output mem_to_reg,
  output ula_src,
  output jump,
  output branch
);

  wire and_1_out, and_2_out, and_3_out, and_4_out, and_5_out, and_6_out, and_10_out, and_11_out, not_1_out,
       not_2_out, not_3_out, not_4_out, not_5_out, not_6_out, not_7_out;

  and and_1 (and_1_out, E3, E0);
  and and_2 (and_2_out, E3, E1);
  and and_3 (and_3_out, E2, E1);
  and and_4 (and_4_out, E3, not_1_out);
  not not_1 (not_1_out, E0);
  and and_5 (and_5_out, E3, E1);
  not not_2 (not_2_out, E3);
  and and_6 (and_6_out, E1, not_3_out);
  not not_3 (not_3_out, E0);
  and and_7 (write_mem, E3, not_4_out, not_5_out);
  not not_4 (not_4_out, E1);
  not not_5 (not_5_out, E0);
  and and_8 (read_mem, E2, E1, E0);
  and and_9 (mem_to_reg, E2, E1, E0);
  and and_10 (and_10_out, E2, E1);
  and and_11 (and_11_out, E3, not_6_out);
  not not_6 (not_6_out, E0);
  and and_12 (jump, E3, E1, E0);
  not not_7 (not_7_out, E1);
  and and_13 (branch, E3, not_7_out, E0);
  or or_1 (ula_op_0, and_1_out, and_2_out);
  or or_2 (ula_op_1, and_3_out, and_4_out, and_5_out);
  or or_3 (write_reg, not_2_out, and_6_out);
  or or_4 (ula_src, and_10_out, and_11_out);
endmodule
